// Logisim project Q6.circ as structural Verilog: 1 circuit, main circuit main
module main (
  input  [3:0] in_1,
  output out_2
);

  wire and_1_out, and_2_out, and_3_out, and_4_out, not_1_out, not_2_out, or_1_out;

  not not_1 (not_1_out, in_1[3]);
  not not_2 (not_2_out, in_1[1]);
  and and_1 (and_1_out, in_1[0], in_1[1]);
  or or_1 (or_1_out, in_1[0], in_1[1]);
  and and_2 (and_2_out, in_1[2], in_1[3]);
  and and_3 (and_3_out, not_1_out, in_1[2], in_1[0], not_2_out);
  and and_4 (and_4_out, or_1_out, and_2_out);
  or or_2 (out_2, and_1_out, and_4_out, and_3_out);

  // Notes on the sheet:
  //   D
  //   C
  //   B
  //   A
endmodule
