// Logisim project q2.circ as structural Verilog: 1 circuit, main circuit main
module main (
  input  [3:0] in_1,
  output [6:0] out_2
);

  ROM #(.addrWidth(4), .dataWidth(7)) rom_1 (.addr(in_1), .data(out_2));  // open: sel

  // Notes on the sheet:
  //   contents of rom_1 (hex, n*v repeats v):
  //   7e 30 6d 79 33 5b 5f 70 7f 7b
endmodule
