// Logisim project Q1.circ as structural Verilog: 1 circuit, main circuit main
module main (
  input  in_1,
  output [1:0] out_2
);

  Counter #(.width(2), .max('h3)) counter_1 (.Q(out_2), .clk(in_1));  // open: load, D, count, carry, clr
endmodule
